// Logisim project primes.circ as structural Verilog: 1 circuit, main circuit main
module main (
  input  [3:0] in_1,
  input  [3:0] in_2
);

  wire nor_1_out, not_1_out;
  wire [3:0] adder_1_out, divider_1_rem;

  Bit_Extender #(.in_width(3), .out_width(4)) bit_extender_1 ();  // open: in, out
  Adder #(.width(4)) adder_1 (.a(in_1), .b(in_2), .out(adder_1_out));  // open: cin, cout
  Hex_Digit_Display hex_digit_display_1 (.value(adder_1_out));  // open: dp
  not not_1 (not_1_out, adder_1_out[0]);
  Divider #(.width(4)) divider_1 (.a(adder_1_out), .b(4'b0011), .rem(divider_1_rem));  // open: out, upper
  Hex_Digit_Display hex_digit_display_2 (.value(divider_1_rem));  // open: dp
  nor nor_1 (nor_1_out, divider_1_rem[0], divider_1_rem[1], divider_1_rem[2], divider_1_rem[3]);
endmodule
